// Logisim project proiect.circ as structural Verilog
module main (
  input  in_1,
  input  in_2,
  input  in_3,
  input  in_4
);

  wire algoritmtimp_1_zi_noua, ceas_1_en0, ceas_1_en1, ceas_1_en2, ceas_1_en3, ceas_1_en4, ceas_1_en5,
       ceas_1_en6, ceas_1_en7, ceas_1_ensetout, ceas_1_incout, ceas_1_setoutdata, ceas_1_setouttimp,
       clock_1_out, clock_2_out, clock_3_out;
  wire [1:0] ceas_1_sel;
  wire [6:0] algoritmdata_1_luna_u_nou, algoritmdata_1_luna_z_nou, algoritmdata_1_zi_u_nou,
       algoritmdata_1_zi_z_nou, algoritmtimp_1_min_u_nou, algoritmtimp_1_min_z_nou, algoritmtimp_1_ora_u_nou,
       algoritmtimp_1_ora_z_nou, ceas_1_ssd1, ceas_1_ssd2, ceas_1_ssd3, ceas_1_ssd4,
       decoderbintossd_1_abcdefg, decoderbintossd_2_abcdefg, decoderbintossd_3_abcdefg,
       decoderbintossd_4_abcdefg, multiplexer_1_out, multiplexer_2_out, multiplexer_3_out, multiplexer_4_out,
       num01_1_numar, num02_1_numar, num03_1_numar, num05_1_numar, num09_1_numar, num09_2_numar,
       num09_3_numar, num09_4_numar;
  wire [14:0] randomm_1_rez;

  Clock clock_1 (.out(clock_1_out));
  Clock clock_2 (.out(clock_2_out));
  ceas ceas_1 (
    .clk4(clock_2_out), .reset(in_1), .start(in_2), .set(in_3), .inc(in_4), .temp(randomm_1_rez),
    .min_u(algoritmtimp_1_min_u_nou), .min_z(algoritmtimp_1_min_z_nou), .ora_u(algoritmtimp_1_ora_u_nou),
    .ora_z(algoritmtimp_1_ora_z_nou), .luna_u(algoritmdata_1_luna_u_nou), .luna_z(algoritmdata_1_luna_z_nou),
    .zi_u(algoritmdata_1_zi_u_nou), .zi_z(algoritmdata_1_zi_z_nou), .ensetout(ceas_1_ensetout),
    .incout(ceas_1_incout), .ssd4(ceas_1_ssd4), .ssd3(ceas_1_ssd3), .ssd2(ceas_1_ssd2), .ssd1(ceas_1_ssd1),
    .en7(ceas_1_en7), .en6(ceas_1_en6), .en5(ceas_1_en5), .en4(ceas_1_en4), .en3(ceas_1_en3),
    .en2(ceas_1_en2), .en1(ceas_1_en1), .en0(ceas_1_en0), .sel(ceas_1_sel), .setouttimp(ceas_1_setouttimp),
    .setoutdata(ceas_1_setoutdata));
  randomm randomm_1 (.clk(clock_1_out), .rez(randomm_1_rez));
  _7_Segment_Display #(.active("false"), .decimalPoint("false")) u_7_segment_display_1 (
    .g(decoderbintossd_1_abcdefg[0]), .f(decoderbintossd_1_abcdefg[1]), .a(decoderbintossd_1_abcdefg[6]),
    .b(decoderbintossd_1_abcdefg[5]), .e(decoderbintossd_1_abcdefg[2]), .d(decoderbintossd_1_abcdefg[3]),
    .c(decoderbintossd_1_abcdefg[4]));
  decoderbintossd decoderbintossd_1 (.bin_in(multiplexer_1_out), .abcdefg(decoderbintossd_1_abcdefg));
  Multiplexer #(.select(2), .width(7)) multiplexer_1 (
    .in0(ceas_1_ssd4), .in1(num02_1_numar), .in2(num01_1_numar), .out(multiplexer_1_out), .sel(ceas_1_sel));  // open: in3
  _7_Segment_Display #(.active("false"), .decimalPoint("false")) u_7_segment_display_2 (
    .g(decoderbintossd_2_abcdefg[0]), .f(decoderbintossd_2_abcdefg[1]), .a(decoderbintossd_2_abcdefg[6]),
    .b(decoderbintossd_2_abcdefg[5]), .e(decoderbintossd_2_abcdefg[2]), .d(decoderbintossd_2_abcdefg[3]),
    .c(decoderbintossd_2_abcdefg[4]));
  num09 num09_1 (.clk(ceas_1_incout), .en(ceas_1_en0), .numar(num09_1_numar));
  num05 num05_1 (.clk(ceas_1_incout), .en(ceas_1_en1), .numar(num05_1_numar));
  num09 num09_2 (.clk(ceas_1_incout), .en(ceas_1_en2), .numar(num09_2_numar));
  num02 num02_1 (.clk(ceas_1_incout), .en(ceas_1_en3), .numar(num02_1_numar));
  num09 num09_3 (.clk(ceas_1_incout), .en(ceas_1_en4), .numar(num09_3_numar));
  num03 num03_1 (.clk(ceas_1_incout), .en(ceas_1_en5), .numar(num03_1_numar));
  num09 num09_4 (.clk(ceas_1_incout), .en(ceas_1_en6), .numar(num09_4_numar));
  num01 num01_1 (.clk(ceas_1_incout), .en(ceas_1_en7), .numar(num01_1_numar));
  decoderbintossd decoderbintossd_2 (.bin_in(multiplexer_2_out), .abcdefg(decoderbintossd_2_abcdefg));
  Multiplexer #(.select(2), .width(7)) multiplexer_2 (
    .in0(ceas_1_ssd3), .in1(num09_2_numar), .in2(num09_4_numar), .out(multiplexer_2_out), .sel(ceas_1_sel));  // open: in3
  _7_Segment_Display #(.active("false"), .decimalPoint("false")) u_7_segment_display_3 (
    .g(decoderbintossd_3_abcdefg[0]), .f(decoderbintossd_3_abcdefg[1]), .a(decoderbintossd_3_abcdefg[6]),
    .b(decoderbintossd_3_abcdefg[5]), .e(decoderbintossd_3_abcdefg[2]), .d(decoderbintossd_3_abcdefg[3]),
    .c(decoderbintossd_3_abcdefg[4]));
  Multiplexer #(.select(2), .width(7)) multiplexer_3 (
    .in0(ceas_1_ssd2), .in1(num05_1_numar), .in2(num03_1_numar), .out(multiplexer_3_out), .sel(ceas_1_sel));  // open: in3
  decoderbintossd decoderbintossd_3 (.bin_in(multiplexer_3_out), .abcdefg(decoderbintossd_3_abcdefg));
  _7_Segment_Display #(.active("false"), .decimalPoint("false")) u_7_segment_display_4 (
    .g(decoderbintossd_4_abcdefg[0]), .f(decoderbintossd_4_abcdefg[1]), .a(decoderbintossd_4_abcdefg[6]),
    .b(decoderbintossd_4_abcdefg[5]), .e(decoderbintossd_4_abcdefg[2]), .d(decoderbintossd_4_abcdefg[3]),
    .c(decoderbintossd_4_abcdefg[4]));
  decoderbintossd decoderbintossd_4 (.bin_in(multiplexer_4_out), .abcdefg(decoderbintossd_4_abcdefg));
  Multiplexer #(.select(2), .width(7)) multiplexer_4 (
    .in0(ceas_1_ssd1), .in1(num09_1_numar), .in2(num09_3_numar), .out(multiplexer_4_out), .sel(ceas_1_sel));  // open: in3
  Clock clock_3 (.out(clock_3_out));
  algoritmtimp algoritmtimp_1 (
    .clk(clock_3_out), .min_u(num09_1_numar), .min_z(num05_1_numar), .ora_u(num09_2_numar),
    .ora_z(num02_1_numar), .en(ceas_1_ensetout), .set(ceas_1_setouttimp),
    .min_u_nou(algoritmtimp_1_min_u_nou), .min_z_nou(algoritmtimp_1_min_z_nou),
    .ora_u_nou(algoritmtimp_1_ora_u_nou), .ora_z_nou(algoritmtimp_1_ora_z_nou),
    .zi_noua(algoritmtimp_1_zi_noua));
  algoritmdata algoritmdata_1 (
    .clk_zi_noua_in(algoritmtimp_1_zi_noua), .zi_u(num09_3_numar), .zi_z(num03_1_numar),
    .luna_u(num09_4_numar), .luna_z(num01_1_numar), .en(ceas_1_ensetout), .set(ceas_1_setoutdata),
    .zi_u_nou(algoritmdata_1_zi_u_nou), .zi_z_nou(algoritmdata_1_zi_z_nou),
    .luna_u_nou(algoritmdata_1_luna_u_nou), .luna_z_nou(algoritmdata_1_luna_z_nou));  // open: an_nou
endmodule

module testdata (
  input  [6:0] in_1,
  input  [6:0] in_2,
  input  [6:0] in_3,
  input  in_4,
  input  [6:0] in_5,
  input  in_6
);

  wire clock_1_out;
  wire [6:0] algoritmdata_1_luna_u_nou, algoritmdata_1_luna_z_nou, algoritmdata_1_zi_u_nou,
       algoritmdata_1_zi_z_nou, decoderbintossd_1_abcdefg, decoderbintossd_2_abcdefg,
       decoderbintossd_3_abcdefg, decoderbintossd_4_abcdefg;

  Clock clock_1 (.out(clock_1_out));
  _7_Segment_Display #(.active("false"), .decimalPoint("false")) u_7_segment_display_1 (
    .g(decoderbintossd_1_abcdefg[0]), .f(decoderbintossd_1_abcdefg[1]), .a(decoderbintossd_1_abcdefg[6]),
    .b(decoderbintossd_1_abcdefg[5]), .e(decoderbintossd_1_abcdefg[2]), .d(decoderbintossd_1_abcdefg[3]),
    .c(decoderbintossd_1_abcdefg[4]));
  decoderbintossd decoderbintossd_1 (.bin_in(algoritmdata_1_luna_z_nou), .abcdefg(decoderbintossd_1_abcdefg));
  algoritmdata algoritmdata_1 (
    .clk_zi_noua_in(clock_1_out), .zi_u(in_1), .zi_z(in_2), .luna_u(in_3), .luna_z(in_5), .en(in_4),
    .set(in_6), .zi_u_nou(algoritmdata_1_zi_u_nou), .zi_z_nou(algoritmdata_1_zi_z_nou),
    .luna_u_nou(algoritmdata_1_luna_u_nou), .luna_z_nou(algoritmdata_1_luna_z_nou));  // open: an_nou
  _7_Segment_Display #(.active("false"), .decimalPoint("false")) u_7_segment_display_2 (
    .g(decoderbintossd_2_abcdefg[0]), .f(decoderbintossd_2_abcdefg[1]), .a(decoderbintossd_2_abcdefg[6]),
    .b(decoderbintossd_2_abcdefg[5]), .e(decoderbintossd_2_abcdefg[2]), .d(decoderbintossd_2_abcdefg[3]),
    .c(decoderbintossd_2_abcdefg[4]));
  decoderbintossd decoderbintossd_2 (.bin_in(algoritmdata_1_luna_u_nou), .abcdefg(decoderbintossd_2_abcdefg));
  _7_Segment_Display #(.active("false"), .decimalPoint("false")) u_7_segment_display_3 (
    .g(decoderbintossd_3_abcdefg[0]), .f(decoderbintossd_3_abcdefg[1]), .a(decoderbintossd_3_abcdefg[6]),
    .b(decoderbintossd_3_abcdefg[5]), .e(decoderbintossd_3_abcdefg[2]), .d(decoderbintossd_3_abcdefg[3]),
    .c(decoderbintossd_3_abcdefg[4]));
  decoderbintossd decoderbintossd_3 (.bin_in(algoritmdata_1_zi_z_nou), .abcdefg(decoderbintossd_3_abcdefg));
  _7_Segment_Display #(.active("false"), .decimalPoint("false")) u_7_segment_display_4 (
    .g(decoderbintossd_4_abcdefg[0]), .f(decoderbintossd_4_abcdefg[1]), .a(decoderbintossd_4_abcdefg[6]),
    .b(decoderbintossd_4_abcdefg[5]), .e(decoderbintossd_4_abcdefg[2]), .d(decoderbintossd_4_abcdefg[3]),
    .c(decoderbintossd_4_abcdefg[4]));
  decoderbintossd decoderbintossd_4 (.bin_in(algoritmdata_1_zi_u_nou), .abcdefg(decoderbintossd_4_abcdefg));
endmodule

// VHDL entity ceas, as the project stores it:
--------------------------------------------------------------------------------
-- Project :
-- File    :
-- Autor   :
-- Date    :
--
--------------------------------------------------------------------------------
-- Description :set asincron,generator,algdata,frecventa clock
--
--------------------------------------------------------------------------------

LIBRARY ieee;
USE ieee.std_logic_1164.all;
USE ieee.std_logic_unsigned.all;

ENTITY ceas IS
  PORT (
 	clk4,reset,start: in std_logic; 
 	set,inc : in std_logic; --iesiri de control pt resurse
 	temp : in std_logic_vector(14 downto 0); --intrari de la resurse
 	min_u,min_z,ora_u,ora_z,luna_u,luna_z,zi_u,zi_z: in std_logic_vector(6 downto 0); -- intrari de la resurse
 	ensetout,incout : out std_logic; --iesiri pt resurse
 	ssd4,ssd3,ssd2,ssd1:out std_logic_vector(6 downto 0); -- iesiri pt utilizator
 	en7,en6,en5,en4,en3,en2,en1,en0 : out std_logic; -- iesiri de control pt resurse
 	sel : out std_logic_vector(1 downto 0);

 	setouttimp:out std_logic;
 	setoutdata:out std_logic
    );
END ceas;

--------------------------------------------------------------------------------
--Complete your VHDL description below
--------------------------------------------------------------------------------

ARCHITECTURE stari_ceas OF ceas IS
type stare_t is (stinit,stsetmin_u,stsetmin_z,stsetora_u,stsetora_z,stsetzi_u,stsetzi_z,stsetluna_u,stsetluna_z,sttmp,sttimp,stdata);
signal stare,nxstare:stare_t;
BEGIN


act_stare : process(clk4,reset)

	begin
		if reset='1' then stare<=stinit;
		elsif clk4'event and clk4 = '1' then 
		stare<=nxstare;
		end if;
	end process act_stare;

tranzitii : process(stare,inc,set,start,min_u,min_z,ora_u,ora_z,luna_u,luna_z,zi_u,zi_z)
begin

	case stare is 
		when stinit=>
				sel<="00";
				ssd4<="0000000";ssd3<="0000000";ssd2<="0000000";ssd1<="0000000";
				en0<='0';en1<='0';en2<='0';en3<='0';en4<='0';en5<='0';en6<='0';en7<='0';
				if start='1' then
				nxstare<=stsetmin_u;
				else nxstare<=stinit;
				end if;
		when stsetmin_u=>
					setouttimp<='1';--pornim setarea timpului
					sel<="01";
					if inc='1' then
					incout<='1';
					else incout<='0';
					end if;
					
					if set='1' then
				en0<='0';
				nxstare<=stsetmin_z;
				else en0<='1';
				nxstare<=stsetmin_u;
				
				end if;
					
		when stsetmin_z=>
				
					sel<="01";
					if inc='1'then
					incout<='1'; 
					else incout<='0';
					end if;
					if set='1' then
					
					en1<='0';
					nxstare<=stsetora_u;
					else en1<='1';
					nxstare<=stsetmin_z;
					end if;
							

		when stsetora_u=>
				
					sel<="01";
					if inc='1'then
					incout<='1'; 
					else incout<='0';
					end if;
					if set='1' then
				
				en2<='0';
				nxstare<=stsetora_z;
				else en2<='1';
				nxstare<=stsetora_u;
				end if;

		when stsetora_z=>

				sel<="01";
				if inc='1'then
					incout<='1'; 
					else incout<='0';
					end if;
				if set='1' then
				
				en3<='0';
				nxstare<=stsetzi_u;
				else en3<='1';
				nxstare<=stsetora_z;
				end if;

	----------------------------------------------------------------
		
		when stsetzi_u=>
		setouttimp<='0';--oprim setarea timpului
		setoutdata<='1';--pornim setarea datei
				sel<="10";
				if inc='1'then
					incout<='1'; 
					else incout<='0';
					end if;
				if set='1' then
				en4<='0';
				nxstare<=stsetzi_z;
				else en4<='1'; 
				nxstare<=stsetzi_u;
				end if;
				
					
		when stsetzi_z=>
				
					sel<="10";
					if inc='1'then
					incout<='1'; 
					else incout<='0';
					end if;
					if set='1' then
				en5<='0';
				nxstare<=stsetluna_u;
				else en5<='1';
				nxstare<=stsetzi_z;
				end if;

		when stsetluna_u=>
				sel<="10";
				if inc='1'then
					incout<='1'; 
					else incout<='0';
					end if;
				if set='1' then
				en6<='0';
				nxstare<=stsetluna_z;
				else en6<='1';
				nxstare<=stsetluna_u;
				end if;
				
		when stsetluna_z=>
				
				sel<="10";
				if inc='1'then
				incout<='1'; 
				else incout<='0';
				end if;
				
					if set='1' then
				en7<='0';	
				
				setoutdata<='0';--oprim setarea datei
				ensetout<='1'; --pornim algoritmii

				nxstare<=sttmp;
				else en7<='1';
				nxstare<=stsetluna_z;
				end if;


------------------------------------------------------			
		
		when sttmp=> 
				   
				   sel<="00";
				   ssd1<=temp(6 downto 0);
				   ssd2<=temp(13 downto 7);
				   if temp(14)='1' then
				   ssd3<="0001010"; -- 10 e minus
				   ssd4<="0001010";
				   else ssd3<="0000000";
				   end if;
				   ssd4<="0000000";
				   nxstare<=sttimp;
				   
		when sttimp =>
					sel<="00";
					ssd1<=min_u;
					ssd2<=min_z;
					ssd3<=ora_u;
					ssd4<=ora_z;
					nxstare<=stdata;
			
		when stdata => 
					sel<="00";
					ssd1<=zi_u;
					ssd2<=zi_z;
					ssd3<=luna_u;
					ssd4<=luna_z;
					nxstare<=sttmp;
		
	end case;
end process tranzitii;
END stari_ceas;

// VHDL entity num09, as the project stores it:
-------------------------------------------------

LIBRARY ieee;
USE ieee.std_logic_1164.all;
USE ieee.std_logic_unsigned.all;
USE ieee.std_logic_arith.all;


ENTITY num09 IS
  PORT (
  ------------------------------------------------------------------------------
	clk : in std_logic;
	en  : in std_logic;
	numar : out std_logic_vector(6 downto 0)
    );
END num09;

--------------------------------------------------------------------------------
--Complete your VHDL description below
--------------------------------------------------------------------------------

ARCHITECTURE TypeArchitecture OF num09 IS

signal temp : std_logic_vector(6 downto 0):=(others=>'0');
BEGIN

process(clk,en)
begin
if temp="0001001" then
temp<="0000000";
elsif clk='1' and clk'event then
	if en = '1' then
		temp <= temp + 1;
	end if;
end if;
end process;

numar <= temp;
END TypeArchitecture;

// VHDL entity decoderbintossd, as the project stores it:
--------------------------------------------------------------------------------
-- Project :
-- File    :
-- Autor   :
-- Date    :
--
--------------------------------------------------------------------------------
-- Description :
--
--------------------------------------------------------------------------------

LIBRARY ieee;
USE ieee.std_logic_1164.all;

ENTITY decoderbintossd IS
  PORT (
  bin_in : in std_logic_vector(6 downto 0);
  abcdefg : out std_logic_vector(6 downto 0)
    );
END decoderbintossd;

--------------------------------------------------------------------------------
--Complete your VHDL description below
--------------------------------------------------------------------------------

ARCHITECTURE TypeArchitecture OF decoderbintossd IS

BEGIN

abcdefg <="0000001" when bin_in="0000000"else
		"1001111" when bin_in="0000001"else
		"0010010" when bin_in="0000010"else
		"0000110" when bin_in="0000011"else
		"1001100" when bin_in="0000100"else
		"0100100" when bin_in="0000101"else
		"0100000" when bin_in="0000110"else
		"0001111" when bin_in="0000111"else
		"0000000" when bin_in="0001000"else
		"0000100" when bin_in="0001001"else
		"1111110" when bin_in="0001010";
		
		

END TypeArchitecture;

// VHDL entity num05, as the project stores it:
--------------------------------------------------------------------------------
-- Project :
-- File    :
-- Autor   :
-- Date    :
--
--------------------------------------------------------------------------------
-- Description :
--
--------------------------------------------------------------------------------

LIBRARY ieee;
USE ieee.std_logic_1164.all;
USE ieee.std_logic_unsigned.all;
USE ieee.std_logic_arith.all;


ENTITY num05 IS
  PORT (
  ------------------------------------------------------------------------------
	clk : in std_logic;
	en  : in std_logic;
	numar : out std_logic_vector(6 downto 0)
    );
END num05;

--------------------------------------------------------------------------------
--Complete your VHDL description below
--------------------------------------------------------------------------------

ARCHITECTURE TypeArchitecture OF num05 IS

signal temp : std_logic_vector(6 downto 0):=(others=>'0');
BEGIN

process(clk,en)
begin

  if  rising_edge(clk) and en='1' then
	if temp="0000101" then
temp<="0000000";
else
	temp <= temp + 1;
	end if;
end if;
end process;

numar <= temp;
END TypeArchitecture;

// VHDL entity randomm, as the project stores it:
--------------------------------------------------------------------------------

LIBRARY ieee;
USE ieee.std_logic_1164.all;
USE ieee.std_logic_unsigned.all;
use ieee.numeric_std.all;


ENTITY randomm IS
  PORT (
 clk:in std_logic;
 rez: out std_logic_vector(14 downto 0)
    );
END randomm;



ARCHITECTURE TypeArchitecture OF randomm IS


BEGIN

process(clk)
 variable num_int : integer;
 variable num_int2 : integer;
  
variable val1:std_logic_vector(6 downto 0):="1000000";
variable val2:std_logic_vector(6 downto 0):="1000010";
begin

if rising_edge(clk) then
	if val1="0000000" then
	val1:=val1+1;
	end if;
	val1(6):=val1(6) xor val1(0);
	val1 (5 downto 0):=val1(6 downto 1);--shiftare
 	num_int := to_integer(unsigned(val1));
 	num_int:= num_int mod 9; 	
	val1:= std_logic_vector(to_unsigned(num_int,7));
	
	
	
	if val2="0000000" then
	val2:=val2+1;
	end if;
	val2(6):=val2(6) xor val2(0);
	val2 (5 downto 0):=val2(6 downto 1);--shiftare
 	num_int := to_integer(unsigned(val2));
 	num_int:= num_int mod 9; 	
	val2:= std_logic_vector(to_unsigned(num_int,7));	
	
	

end if;
rez<=val1(0)&val1 & val2;

	end process;

END TypeArchitecture;

// VHDL entity algoritmtimp, as the project stores it:
--------------------------------------------------------------------------------
-- Project :
-- File    :
-- Autor   :
-- Date    :
--
--------------------------------------------------------------------------------
-- Description :
--
--------------------------------------------------------------------------------

LIBRARY ieee;
USE ieee.std_logic_1164.all;
USE ieee.std_logic_unsigned.all;


ENTITY algoritmtimp IS
  PORT (
  	   clk: in std_logic;
        min_u, min_z, ora_u, ora_z: in std_logic_vector(6 downto 0);
        min_u_nou, min_z_nou, ora_u_nou, ora_z_nou: out std_logic_vector(6 downto 0);
        en:in std_logic;
        set:in std_logic;
        zi_noua: out std_logic
    );
END algoritmtimp;

--------------------------------------------------------------------------------
--Complete your VHDL description below
--------------------------------------------------------------------------------

ARCHITECTURE TypeArchitecture OF algoritmtimp IS
	
	   signal min_u_nou_var: std_logic_vector(6 downto 0):="ZZZZZZZ";
        signal min_z_nou_var: std_logic_vector(6 downto 0):="ZZZZZZZ";
        signal ora_u_nou_var: std_logic_vector(6 downto 0):="ZZZZZZZ";
        signal ora_z_nou_var: std_logic_vector(6 downto 0):="ZZZZZZZ";
        signal zi_noua_sig :std_logic:='0';

begin
process(clk,set)

    begin
    if(set='1') then

				min_u_nou_var<=min_u;
				min_z_nou_var<=min_z;
				ora_u_nou_var<=ora_u;
				ora_z_nou_var<=ora_z;
			else
        if rising_edge(clk) then
            
            if en='1' then
            if zi_noua_sig='1'then
            zi_noua<='0';
            zi_noua_sig<='0';
            end if;
            if min_u_nou_var = "0001001" then
                min_u_nou_var <= "0000000";
                
                if min_z_nou_var = "0000101" then
                    min_z_nou_var <= "0000000";
                    
                    if ora_u_nou_var = "0000011" then
                   		 ora_u_nou_var <= "0000000";
                        if ora_z_nou_var = "0000010" then
                            ora_z_nou_var <= "0000000";
                            zi_noua <= '1';
                            zi_noua_sig<='1';
                        else
                            ora_u_nou_var <= ora_u_nou_var + 1; 
                        end if;
                    else
                        if ora_u_nou_var = "0001001" then
                            ora_z_nou_var <= ora_z_nou_var + 1;
                            ora_u_nou_var <= "0000000";
                        else
                            ora_u_nou_var <= ora_u_nou_var + 1;
                        end if;
                    end if;
                else
                    min_z_nou_var <= min_z_nou_var + 1;
                end if;
            else
                min_u_nou_var <=min_u_nou_var + 1; 
            end if;
            end if;
           end if;
        end if;
        	
    end process;
            min_u_nou <= min_u_nou_var;
            min_z_nou <= min_z_nou_var;
            ora_u_nou <= ora_u_nou_var;
            ora_z_nou <= ora_z_nou_var;

END TypeArchitecture;

// VHDL entity algoritmdata, as the project stores it:
--------------------------------------------------------------------------------

-- Project :

-- File    :

-- Autor   :
 
-- Date    :

--

--------------------------------------------------------------------------------

-- Description :

--

--------------------------------------------------------------------------------



LIBRARY ieee;

USE ieee.std_logic_1164.all;

USE ieee.std_logic_unsigned.all;

ENTITY algoritmdata IS

  PORT (
    clk_zi_noua_in:in std_logic;

    zi_u, zi_z, luna_u, luna_z: in std_logic_vector(6 downto 0);
    zi_u_nou, zi_z_nou, luna_u_nou, luna_z_nou: out std_logic_vector(6 downto 0);
    en, set: in std_logic;
    an_nou: out std_logic
    );

END algoritmdata;



--------------------------------------------------------------------------------

--Complete your VHDL description below

--------------------------------------------------------------------------------



ARCHITECTURE TypeArchitecture OF algoritmdata IS

    
       
BEGIN

    
    
    
process(clk_zi_noua_in,set,zi_z,zi_u,luna_u,luna_z)
       variable zi_u_nou_sig: std_logic_vector(6 downto 0);
        variable zi_z_nou_sig: std_logic_vector(6 downto 0);
        variable luna_u_nou_sig: std_logic_vector(6 downto 0);
        variable luna_z_nou_sig: std_logic_vector(6 downto 0);
   begin
   if set='1' then

                zi_u_nou_sig:=zi_u;
                zi_z_nou_sig:=zi_z;
                luna_u_nou_sig:=luna_u;
                luna_z_nou_sig:=luna_z;    
                else
                
      if falling_edge(clk_zi_noua_in) then     
      
       if en='1' then
         if (luna_u_nou_sig = "0000010" and luna_z_nou_sig = "0000001") then
                if (zi_z_nou_sig = "0000011" and zi_u_nou_sig = "0000001") then
                    an_nou <='1';
                    zi_u_nou_sig := "0000001";
                    zi_z_nou_sig := "0000000";
                    luna_u_nou_sig := "0000001";
                    luna_z_nou_sig := "0000000";
                elsif (zi_u_nou_sig = "0001001") then
                    zi_u_nou_sig:="0000000";
                        zi_z_nou_sig := zi_z_nou_sig +1;
                else
                    zi_z_nou_sig := zi_z_nou_sig + 1;
                end if;
                
            elsif (luna_u_nou_sig = "0000001" and luna_z_nou_sig = "0000000") or
                  (luna_u_nou_sig = "0000011" and luna_z_nou_sig = "0000000") or
                  (luna_u_nou_sig = "0000101" and luna_z_nou_sig = "0000000") or
                  (luna_u_nou_sig = "0000111" and luna_z_nou_sig = "0000000") or
                  (luna_u_nou_sig = "0001000" and luna_z_nou_sig = "0000000") then
                if (zi_z_nou_sig = "0000011" and zi_u_nou_sig = "0000001") then
                    zi_z_nou_sig := "0000000";
                    zi_u_nou_sig := "0000001";
                    luna_u_nou_sig := luna_u_nou_sig + 1;
                else
                    if (zi_u_nou_sig = "0001001") then
                        zi_u_nou_sig:="0000000";
                        zi_z_nou_sig := zi_z_nou_sig +1;
                    else
                        zi_u_nou_sig := zi_u_nou_sig + 1;
                       
                    end if;
                end if;
                
            elsif (luna_u_nou_sig = "0000000" and luna_z_nou_sig = "0000001") then
                if (zi_z_nou_sig = "0000011" and zi_u_nou_sig = "0000001") then
                    zi_z_nou_sig := "0000000";
                    zi_u_nou_sig := "0000001";
                    luna_u_nou_sig := luna_u_nou_sig + 1;
                else
                    if (zi_u_nou_sig = "0001001") then
                    zi_u_nou_sig:="0000000";
                        zi_z_nou_sig := zi_z_nou_sig +1;
                    else
                        zi_u_nou_sig := zi_u_nou_sig + 1;
                    end if;
                end if;
                
            elsif (luna_u_nou_sig = "0000010" and luna_z_nou_sig = "0000000") then
                if (zi_z_nou_sig = "0000010" and zi_u_nou_sig = "0001000") then
                    zi_z_nou_sig := "0000000";
                    zi_u_nou_sig := "0000001";
                    luna_u_nou_sig := luna_u_nou_sig + 1;
                else
                    if (zi_u_nou_sig = "0001001") then
                    zi_u_nou_sig:="0000000";
                        zi_z_nou_sig := zi_z_nou_sig +1;
                    else
                        zi_u_nou_sig := zi_u_nou_sig + 1;
                    end if;
                end if;
                
            elsif (luna_u_nou_sig = "0000100" and luna_z_nou_sig = "0000000") or
                  (luna_u_nou_sig = "0000110" and luna_z_nou_sig = "0000000") then
                if (zi_z_nou_sig = "0000011" and zi_u_nou_sig = "0000000") then
                    zi_z_nou_sig := "0000000";
                    zi_u_nou_sig := "0000001";
                    luna_u_nou_sig := luna_u_nou_sig + 1;
                else
                    if (zi_u_nou_sig = "0001001") then
                    zi_u_nou_sig:="0000000";
                        zi_z_nou_sig := zi_z_nou_sig +1;
                    else
                        zi_u_nou_sig := zi_u_nou_sig + 1;
                    end if;
                end if;
                
            elsif (luna_u_nou_sig = "0001001" and luna_z_nou_sig = "0000000") then
                if (zi_z_nou_sig = "0000011" and zi_u_nou_sig = "0000000") then
                    zi_z_nou_sig := "0000000";
                    zi_u_nou_sig := "0000001";
                    luna_u_nou_sig := "0000000";
                    luna_z_nou_sig := "0000001";
                else
                    if (zi_u_nou_sig = "0001001") then
                    zi_u_nou_sig:="0000000";
                        zi_z_nou_sig := zi_z_nou_sig +1;
                    else
                        zi_u_nou_sig := zi_u_nou_sig + 1;
                    end if;
                end if;
                
            elsif (luna_u_nou_sig = "0000001" and luna_z_nou_sig = "0000001") then
                if (zi_z_nou_sig = "0000011" and zi_u_nou_sig = "0000000") then
                    zi_z_nou_sig := "0000000";
                    zi_u_nou_sig := "0000001";
                    luna_u_nou_sig := "0000010";
                    luna_z_nou_sig := "0000001";
                else
                    if (zi_u_nou_sig = "0001001") then
                    zi_u_nou_sig:="0000000";
                        zi_z_nou_sig := zi_z_nou_sig +1;
                    else
                        zi_u_nou_sig := zi_u_nou_sig + 1;
                    end if;
                end if;
                
            end if;
       end if;
    end if;
     end if;
            zi_u_nou<=zi_u_nou_sig;
        zi_z_nou<=zi_z_nou_sig;
        luna_u_nou<=luna_u_nou_sig;
        luna_z_nou<=luna_z_nou_sig;
    end process;
    
            

END TypeArchitecture;

// VHDL entity num02, as the project stores it:
--------------------------------------------------------------------------------
-- Project :
-- File    :
-- Autor   :
-- Date    :
--
--------------------------------------------------------------------------------
-- Description :
--
--------------------------------------------------------------------------------

LIBRARY ieee;
USE ieee.std_logic_1164.all;
USE ieee.std_logic_unsigned.all;
USE ieee.std_logic_arith.all;


ENTITY num02 IS
  PORT (
  ------------------------------------------------------------------------------
	clk : in std_logic;
	en  : in std_logic;
	numar : out std_logic_vector(6 downto 0)
    );
END num02;

--------------------------------------------------------------------------------
--Complete your VHDL description below
--------------------------------------------------------------------------------

ARCHITECTURE TypeArchitecture OF num02 IS

signal temp : std_logic_vector(6 downto 0):=(others=>'0');
BEGIN

process(clk,en)
begin

  if  rising_edge(clk) and en='1' then
	if temp="0000010" then
temp<="0000000";
else
	temp <= temp + 1;
	end if;
end if;
end process;
numar <= temp;
END TypeArchitecture;

// VHDL entity num03, as the project stores it:
--------------------------------------------------------------------------------
-- Project :
-- File    :
-- Autor   :
-- Date    :
--
--------------------------------------------------------------------------------
-- Description :
--
--------------------------------------------------------------------------------

LIBRARY ieee;
USE ieee.std_logic_1164.all;
USE ieee.std_logic_unsigned.all;
USE ieee.std_logic_arith.all;


ENTITY num03 IS
  PORT (
  ------------------------------------------------------------------------------
	clk : in std_logic;
	en  : in std_logic;
	numar : out std_logic_vector(6 downto 0)
    );
END num03;

--------------------------------------------------------------------------------
--Complete your VHDL description below
--------------------------------------------------------------------------------

ARCHITECTURE TypeArchitecture OF num03 IS

signal temp : std_logic_vector(6 downto 0):=(others=>'0');
BEGIN

process(clk,en)
begin

  if  rising_edge(clk) and en='1' then
	if temp="0000011" then
temp<="0000000";
else
	temp <= temp + 1;
	end if;
end if;
end process;

numar <= temp;
END TypeArchitecture;

// VHDL entity num01, as the project stores it:
--------------------------------------------------------------------------------
-- Project :
-- File    :
-- Autor   :
-- Date    :
--
--------------------------------------------------------------------------------
-- Description :
--
--------------------------------------------------------------------------------

LIBRARY ieee;
USE ieee.std_logic_1164.all;
USE ieee.std_logic_unsigned.all;
USE ieee.std_logic_arith.all;


ENTITY num01 IS
  PORT (
  ------------------------------------------------------------------------------
	clk : in std_logic;
	en  : in std_logic;
	numar : out std_logic_vector(6 downto 0)
    );
END num01;

--------------------------------------------------------------------------------
--Complete your VHDL description below
--------------------------------------------------------------------------------

ARCHITECTURE TypeArchitecture OF num01 IS

signal temp : std_logic_vector(6 downto 0):=(others=>'0');
BEGIN

process(clk,en)
begin

  if  rising_edge(clk) and en='1' then
	if temp="0000001" then
temp<="0000000";
else
	temp <= temp + 1;
	end if;
end if;
end process;

numar <= temp;
END TypeArchitecture;
